# Fritzing sketch pot-fade (saved by Fritzing 0.7.11b)
breadboards: 1

parts:
  Ard = Arduino
  330Ω = Resistor [tolerance=±5% resistance=330 package=THT]
  LED = LED - 5mm [color="Red (633nm)" package="5 mm [THT]"]
  10kΩ = Rotary Potentiometer (Small) [maximum_resistance=100kΩ]

nets:
  N1: Ard.GND, 330Ω.Pin_0, 10kΩ.leg1
  N2: Ard.D9, LED.anode
  N3: Ard.+5V, 10kΩ.leg2
  N4: Ard.A0, 10kΩ.wiper
  N5: 330Ω.Pin_1, LED.cathode
